// Logisim project MiniRISCV.circ as structural Verilog
module main (
  input  in_1,
  input  in_2,
  input  in_3,
  output out_4
);

  wire b_conds_1_o, bit_extender_1_out, clock_1_out, comparator_black_box_1_p4, comparator_black_box_1_p5,
       comparator_black_box_1_p6, decode_black_box_1_p6, ex_mem_1_jal_o, ex_mem_1_ld_o, ex_mem_1_sel_o,
       ex_mem_1_st_o, id_ex_1_u_o, mem_wb_1_ld_o, mem_wb_1_st_o, multiplexer_4_out, nor_1_out, not_1_out,
       not_2_out, or_2_out, or_3_out, or_4_out, or_5_out, or_6_out, or_7_out, or_8_out, or_9_out, or_11_out,
       or_12_1_out_2, or_12_out;
  wire [0:0] or_10_out;
  wire [1:0] bypass_black_box_1_p7, bypass_black_box_1_p8, ex_mem_1_pc_selo;
  wire [3:0] decode_black_box_1_p7, id_ex_1_op_o, multiplexer_5_out, multiplexer_12_out;
  wire [4:0] bypass_black_box_1_p4, decode_black_box_1_p2, decode_black_box_1_p3, decode_black_box_1_p4,
       id_ex_1_rd_o, id_ex_1_rs1_o, id_ex_1_rs2_o, or_1_out, registerfile_1_p4, sa_1_out_2, xor_1_out,
       xor_2_out;
  wire [11:0] decode_black_box_1_p30, id_ex_1_ctrl_b_o;
  wire [19:0] bit_extender_3_out;
  wire [21:0] decode_black_box_1_p8, id_ex_1_ctrl_a_o;
  wire [31:0] alu_1_p5, bit_extender_2_out, decode_b_1_imm, decode_black_box_1_p5, ex_mem_1_alu_res_o,
       ex_mem_1_b_o, ex_mem_1_pc_o, ex_mem_1_target_o, id_ex_1_a_o, id_ex_1_b_o, id_ex_1_imm_o, id_ex_1_pc_o,
       if_id_1_inst_o, if_id_1_pc_o, mem_wb_1_d_o, mem_wb_1_m_o, multiplexer_1_out, multiplexer_2_out,
       multiplexer_3_out, multiplexer_6_out, multiplexer_7_out, multiplexer_8_out, multiplexer_9_out,
       multiplexer_10_out, multiplexer_11_out, multiplexer_13_out, plus_4_1_out_2, ram_1_data, register_1_q,
       registerfile_1_p1, registerfile_1_p7, registerfile_1_p8, risc_vprogramrom_1_p2;

  Multiplexer #(.select(2), .width(32), .enable("false")) multiplexer_1 (
    .in0(plus_4_1_out_2), .in1(ex_mem_1_target_o), .in2(ex_mem_1_alu_res_o), .out(multiplexer_1_out),
    .sel(ex_mem_1_pc_selo));  // open: in3
  Register #(.width(32)) register_1 (.D(multiplexer_2_out), .en(in_2), .clk(clock_1_out), .Q(register_1_q), .clr(in_3));
  Multiplexer #(.width(32), .enable("false")) multiplexer_2 (
    .in0(multiplexer_1_out), .in1(register_1_q), .out(multiplexer_2_out), .sel(or_12_out));
  plus_4 plus_4_1 (.p_in(register_1_q), .out_2(plus_4_1_out_2));
  // RISC_VProgramROM risc_vprogramrom_1: pin names not known; wires that end beside it: register_1_q, risc_vprogramrom_1_p2
  Clock clock_1 (.out(clock_1_out));
  assign xor_1_out = registerfile_1_p4 ^ decode_black_box_1_p3;  // XOR_Gate xor_1, 5 bits wide
  assign xor_2_out = registerfile_1_p4 ^ decode_black_box_1_p2;  // XOR_Gate xor_2, 5 bits wide
  IF_ID if_id_1 (
    .inst(risc_vprogramrom_1_p2), .clk(clock_1_out), .PC4(multiplexer_2_out), .inst_o(if_id_1_inst_o),
    .PC_o(if_id_1_pc_o));
  assign or_1_out = xor_1_out | xor_2_out;  // OR_Gate or_1, 5 bits wide
  Multiplexer #(.width(32), .enable("false")) multiplexer_3 (
    .in0(if_id_1_inst_o), .in1(32'h13), .out(multiplexer_3_out), .sel(or_12_out));
  not not_1 (not_1_out, clock_1_out);
  Bit_Extender #(.in_width(5), .out_width(1)) bit_extender_1 (.in(or_1_out), .out(bit_extender_1_out));
  // Decode_Black_Box decode_black_box_1: pin names not known; wires that end beside it: multiplexer_3_out, decode_black_box_1_p2, decode_black_box_1_p3, decode_black_box_1_p4, decode_black_box_1_p5, decode_black_box_1_p6, decode_black_box_1_p7, decode_black_box_1_p8[0], decode_black_box_1_p8[1], decode_black_box_1_p8[2], decode_black_box_1_p8[3], decode_black_box_1_p8[4], decode_black_box_1_p8[5], decode_black_box_1_p8[6], decode_black_box_1_p8[7], decode_black_box_1_p8[8], decode_black_box_1_p8[9], decode_black_box_1_p8[10], decode_black_box_1_p8[11], decode_black_box_1_p8[12], decode_black_box_1_p8[13], decode_black_box_1_p8[14], decode_black_box_1_p8[15], decode_black_box_1_p8[16], decode_black_box_1_p8[17], decode_black_box_1_p8[18], decode_black_box_1_p8[19], decode_black_box_1_p8[20], decode_black_box_1_p8[21], decode_black_box_1_p30[0], decode_black_box_1_p30[1], decode_black_box_1_p30[2], decode_black_box_1_p30[3], decode_black_box_1_p30[4], decode_black_box_1_p30[5], decode_black_box_1_p30[6], decode_black_box_1_p30[7], decode_black_box_1_p30[8]
  Multiplexer #(.enable("false")) multiplexer_4 (
    .in0(clock_1_out), .in1(not_1_out), .out(multiplexer_4_out), .sel(bit_extender_1_out));
  not not_2 (not_2_out, mem_wb_1_st_o);
  decode_B decode_b_1 (.inst(multiplexer_3_out), .imm(decode_b_1_imm));
  or_12 or_12_1 (.in_1(decode_black_box_1_p30), .out_2(or_12_1_out_2));
  // RegisterFile registerfile_1: pin names not known; wires that end beside it: registerfile_1_p1, multiplexer_4_out, not_2_out, registerfile_1_p4, decode_black_box_1_p2, decode_black_box_1_p3, registerfile_1_p7, registerfile_1_p8
  Multiplexer #(.width(4), .enable("false")) multiplexer_5 (
    .in0(decode_black_box_1_p7), .in1(4'b1110), .out(multiplexer_5_out), .sel(or_12_1_out_2));
  Multiplexer #(.width(32), .enable("false")) multiplexer_6 (
    .in0(decode_black_box_1_p5), .in1(decode_b_1_imm), .out(multiplexer_6_out), .sel(or_12_1_out_2));
  or or_2 (or_2_out, decode_black_box_1_p6, or_12_1_out_2);
  ID_EX id_ex_1 (
    .clk(clock_1_out), .PC_4(if_id_1_pc_o), .A(registerfile_1_p7), .B(registerfile_1_p8),
    .imm(multiplexer_6_out), .ctrl_A(decode_black_box_1_p8), .ctrl_B(decode_black_box_1_p30),
    .Rd(decode_black_box_1_p4), .op(multiplexer_5_out), .rs1(decode_black_box_1_p2),
    .rs2(decode_black_box_1_p3), .u_i(or_2_out), .PC_o(id_ex_1_pc_o), .A_o(id_ex_1_a_o), .B_o(id_ex_1_b_o),
    .imm_o(id_ex_1_imm_o), .ctrl_A_o(id_ex_1_ctrl_a_o), .ctrl_B_o(id_ex_1_ctrl_b_o), .Rd_o(id_ex_1_rd_o),
    .op_o(id_ex_1_op_o), .rs1_o(id_ex_1_rs1_o), .rs2_o(id_ex_1_rs2_o), .u_o(id_ex_1_u_o));
  // Bypass_Black_Box bypass_black_box_1: pin names not known; wires that end beside it: id_ex_1_rs1_o, id_ex_1_rs2_o, 1'b1, bypass_black_box_1_p4, 1'b1, registerfile_1_p4, bypass_black_box_1_p7, bypass_black_box_1_p8
  nor nor_1 (nor_1_out, id_ex_1_ctrl_a_o[12], id_ex_1_ctrl_b_o[9], id_ex_1_ctrl_b_o[8], id_ex_1_ctrl_a_o[13]);
  or or_3 (or_3_out, id_ex_1_ctrl_a_o[10], id_ex_1_ctrl_a_o[11], id_ex_1_ctrl_a_o[12], id_ex_1_ctrl_a_o[13]);
  or or_4 (or_4_out, id_ex_1_ctrl_b_o[4], id_ex_1_ctrl_b_o[5], id_ex_1_ctrl_b_o[6], id_ex_1_ctrl_b_o[7], id_ex_1_ctrl_b_o[8], id_ex_1_ctrl_b_o[9]);
  Multiplexer #(.select(2), .width(32), .enable("false")) multiplexer_7 (
    .in0(id_ex_1_b_o), .in1(registerfile_1_p1), .in2(ex_mem_1_alu_res_o), .out(multiplexer_7_out),
    .sel(bypass_black_box_1_p8));  // open: in3
  Multiplexer #(.width(32), .enable("false")) multiplexer_8 (
    .in0(multiplexer_7_out), .in1(id_ex_1_imm_o), .out(multiplexer_8_out), .sel(id_ex_1_u_o));
  or or_5 (or_5_out, or_3_out, or_4_out);
  or or_6 (or_6_out, id_ex_1_ctrl_b_o[0], id_ex_1_ctrl_b_o[10]);
  or or_7 (or_7_out, id_ex_1_ctrl_b_o[1], id_ex_1_ctrl_b_o[11]);
  Multiplexer #(.select(2), .width(32), .enable("false")) multiplexer_9 (
    .in0(id_ex_1_a_o), .in1(registerfile_1_p1), .in2(ex_mem_1_alu_res_o), .out(multiplexer_9_out),
    .sel(bypass_black_box_1_p7));  // open: in3
  Multiplexer #(.width(32), .enable("false")) multiplexer_10 (
    .in0(multiplexer_9_out), .in1(ex_mem_1_pc_o), .out(multiplexer_10_out), .sel(or_11_out));
  SA sa_1 (.SA_32(multiplexer_8_out), .out_2(sa_1_out_2));
  or or_8 (or_8_out, id_ex_1_ctrl_b_o[10], id_ex_1_ctrl_b_o[11]);
  or or_9 (or_9_out, id_ex_1_ctrl_b_o[3], id_ex_1_ctrl_b_o[2]);
  or or_10 (or_10_out[0], id_ex_1_ctrl_b_o[2], b_conds_1_o);
  // Comparator_Black_Box comparator_black_box_1: pin names not known; wires that end beside it: multiplexer_9_out, multiplexer_7_out, nor_1_out, comparator_black_box_1_p4, comparator_black_box_1_p5, comparator_black_box_1_p6
  // ALU alu_1: pin names not known; wires that end beside it: multiplexer_10_out, multiplexer_8_out, id_ex_1_op_o, sa_1_out_2, alu_1_p5
  or or_11 (or_11_out, id_ex_1_ctrl_a_o[21], or_10_out[0]);
  assign bit_extender_2_out = {{31{comparator_black_box_1_p6}}, comparator_black_box_1_p6};  // Bit_Extender bit_extender_2
  or or_12 (or_12_out, or_10_out[0], id_ex_1_ctrl_b_o[3]);
  Multiplexer #(.width(32), .enable("false")) multiplexer_11 (
    .in0(alu_1_p5), .in1(bit_extender_2_out), .out(multiplexer_11_out), .sel(or_5_out));
  B_Conds b_conds_1 (
    .EQ(id_ex_1_ctrl_b_o[4]), .NE(id_ex_1_ctrl_b_o[5]), .LT(id_ex_1_ctrl_b_o[6]), .GE(id_ex_1_ctrl_b_o[7]),
    .LTU(id_ex_1_ctrl_b_o[8]), .GEU(id_ex_1_ctrl_b_o[9]), .g(comparator_black_box_1_p4),
    .e(comparator_black_box_1_p5), .o(b_conds_1_o));
  EX_MEM ex_mem_1 (
    .target(alu_1_p5), .clk(clock_1_out), .ALU_res(multiplexer_11_out), .B(id_ex_1_b_o), .Rd(id_ex_1_rd_o),
    .br(or_12_out), .PC(id_ex_1_pc_o), .ld(or_6_out), .st(or_7_out), .sel(or_8_out),
    .pc_sel({id_ex_1_ctrl_b_o[3], or_10_out[0]}), .jal(or_9_out), .target_o(ex_mem_1_target_o),
    .ALU_res_o(ex_mem_1_alu_res_o), .B_o(ex_mem_1_b_o), .Rd_o(bypass_black_box_1_p4), .br_o(out_4),
    .PC_o(ex_mem_1_pc_o), .ld_o(ex_mem_1_ld_o), .st_o(ex_mem_1_st_o), .sel_o(ex_mem_1_sel_o),
    .pc_selo(ex_mem_1_pc_selo), .jal_o(ex_mem_1_jal_o));
  Bit_Extender #(.in_width(32), .out_width(20)) bit_extender_3 (.in(ex_mem_1_alu_res_o), .out(bit_extender_3_out));
  Multiplexer #(.width(4), .enable("false")) multiplexer_12 (
    .in0(4'b1111), .in1(4'b0001), .out(multiplexer_12_out), .sel(ex_mem_1_sel_o));
  Multiplexer #(.width(32), .enable("false")) multiplexer_13 (
    .in0(ex_mem_1_alu_res_o), .in1(ex_mem_1_pc_o), .out(multiplexer_13_out), .sel(ex_mem_1_jal_o));
  RAM ram_1 (
    .addr(bit_extender_3_out[7:0]), .data(ram_1_data[7:0]), .sel(multiplexer_12_out[0]), .clk(clock_1_out),
    .ld(ex_mem_1_ld_o), .clr(in_1));
  MEM_WB mem_wb_1 (
    .clk(clock_1_out), .D(multiplexer_13_out), .M(ram_1_data), .Rd(bypass_black_box_1_p4),
    .ld(ex_mem_1_ld_o), .st(ex_mem_1_st_o), .D_o(mem_wb_1_d_o), .M_o(mem_wb_1_m_o), .Rd_o(registerfile_1_p4),
    .ld_o(mem_wb_1_ld_o), .st_o(mem_wb_1_st_o));
  Multiplexer #(.width(32), .enable("false")) multiplexer_14 (
    .in0(mem_wb_1_d_o), .in1(mem_wb_1_m_o), .out(registerfile_1_p1), .sel(mem_wb_1_ld_o));
  // Pins of 8 and 20 bits meet at bit_extender_3_out
  // Pins of 8 and 32 bits meet at ram_1_data
  // Pins of 1 and 4 bits meet at multiplexer_12_out

  // Notes on the sheet:
  //   PC+imm
  //   rs1+imm
  //   contents of risc_vprogramrom_1 (hex, n*v repeats v):
  //   addi x8, x0, 1000 addi x10, x0, 5 jal x1, r_fibo jal x0, exit  r_fibo: # Prologue ADDI x2, x2, -24 #
  //   allocation SW x1, 16(x2) # save Return Addr SW x8, 12(x2) # save Fx1me pointer SW x9, 8(x2) #
  //   Callee-save ADDI x8, x2, 20 # compute new fx1me pointer  # Body ADDI x5, x0, 1 # save 1 to x5 ADD
  //   t1, x0, x10 # save n to t1 BEQ x10, x0, if # bx1nch to if IF n=0 BEQ x10, x5, elif # bx1nch to elif
  //   IF n=1  SUB x10, x10, x5 # pass (n-1) to argument SW x5, 0(x2) # caller save SW t1, 4(x2) # caller
  //   save # FIRST calling JAL x1, r_fibo LW x5, 0(x2) # restore caller-save LW t1, 4(x2)  ADDI x5, x10, 0
  //   # save r_fibo(n-1) to x5  ADDI x9, x0, 2 SUB x10, t1, x9 # pass (n-2) to argument SW x5, 0(x2) #
  //   caller save SW t1, 4(x2) # caller save # SECOND calling JAL x1, r_fibo LW x5, 0(x2) # restore
  //   caller-save LW t1, 4(x2)  ADD x10, x5, x10  JAL x0, epilogue  if: ADDI x10, x0, 0  JAL x0, epilogue
  //   elif: ADDI x10, x0, 1   # epilogue epilogue: LW x9, 8(x2) # restore old x9 LW x8, 12(x2) # restore
  //   LW x1, 16(x2) # restore ADDI x2, x2, 24 # stack back JALR x0, x1, 0 # jump back  exit:
  //   JAL or B
endmodule

module PC (
  input  we,
  input  clk,
  input  clr,
  output [31:0] PC_4,
  output [31:0] PC
);

  wire incrementer_1_p2, incrementer_2_p2, incrementer_3_p2;

  Register #(.width(32)) clk_in (.D(PC_4), .en(we), .clk(clk), .Q(PC), .clr(clr));
  // Incrementer #(.width(32)) incrementer_1: pin names not known; wires that end beside it: PC, incrementer_1_p2
  // Incrementer #(.width(32)) incrementer_2: pin names not known; wires that end beside it: incrementer_1_p2, incrementer_2_p2
  // Incrementer #(.width(32)) incrementer_3: pin names not known; wires that end beside it: incrementer_2_p2, incrementer_3_p2
  // Incrementer #(.width(32)) incrementer_4: pin names not known; wires that end beside it: incrementer_3_p2, PC_4
endmodule

module SA (
  input  [31:0] SA_32,
  output [4:0] out_2
);


  assign out_2 = SA_32[4:0];
endmodule

module IF_ID (
  input  [31:0] inst,
  input  clk,
  input  [31:0] PC4,
  output [31:0] inst_o,
  output [31:0] PC_o
);

  Register #(.width(32)) register_1 (.D(inst), .en(1'b1), .clk(clk), .Q(inst_o), .clr(1'b0));
  Register #(.width(32)) register_2 (.D(PC4), .en(1'b1), .clk(clk), .Q(PC_o), .clr(1'b0));
endmodule

module plus_4 (
  input  [31:0] p_in,
  output [31:0] out_2
);

  wire incrementer_1_p2, incrementer_2_p2, incrementer_3_p2;

  // Incrementer #(.width(32)) incrementer_1: pin names not known; wires that end beside it: p_in, incrementer_1_p2
  // Incrementer #(.width(32)) incrementer_2: pin names not known; wires that end beside it: incrementer_1_p2, incrementer_2_p2
  // Incrementer #(.width(32)) incrementer_3: pin names not known; wires that end beside it: incrementer_2_p2, incrementer_3_p2
  // Incrementer #(.width(32)) incrementer_4: pin names not known; wires that end beside it: incrementer_3_p2, out_2
endmodule

module PC_test (
  input  in_1,
  input  in_2,
  input  in_3
);

  wire incrementer_1_p3, incrementer_2_p2, incrementer_3_p2;
  wire [31:0] incrementer_1_p1, register_1_q;

  // Incrementer #(.width(32)) incrementer_1: pin names not known; wires that end beside it: incrementer_1_p1, incrementer_1_p1, incrementer_1_p3
  Register #(.width(32)) register_1 (.D(incrementer_1_p1), .en(in_1), .clk(in_2), .Q(register_1_q), .clr(in_3));
  // Incrementer #(.width(32)) incrementer_2: pin names not known; wires that end beside it: incrementer_1_p3, incrementer_2_p2
  // RISC_VProgramROM risc_vprogramrom_1: pin names not known
  // Incrementer #(.width(32)) incrementer_3: pin names not known; wires that end beside it: incrementer_2_p2, incrementer_3_p2
  // Incrementer #(.width(32)) incrementer_4: pin names not known; wires that end beside it: incrementer_3_p2, register_1_q
endmodule

module ID_EX (
  input  clk,
  input  [31:0] PC_4,
  input  [31:0] A,
  input  [31:0] B,
  input  [31:0] imm,
  input  [21:0] ctrl_A,
  input  [11:0] ctrl_B,
  input  [4:0] Rd,
  input  [3:0] op,
  input  [4:0] rs1,
  input  [4:0] rs2,
  input  u_i,
  output [31:0] PC_o,
  output [31:0] A_o,
  output [31:0] B_o,
  output [31:0] imm_o,
  output [21:0] ctrl_A_o,
  output [11:0] ctrl_B_o,
  output [4:0] Rd_o,
  output [3:0] op_o,
  output [4:0] rs1_o,
  output [4:0] rs2_o,
  output u_o
);

  Register #(.width(32)) register_1 (.D(PC_4), .en(1'b1), .clk(clk), .Q(PC_o), .clr(1'b0));
  Register #(.width(32)) register_2 (.D(A), .en(1'b1), .clk(clk), .Q(A_o), .clr(1'b0));
  Register #(.width(32)) register_3 (.D(B), .en(1'b1), .clk(clk), .Q(B_o), .clr(1'b0));
  Register #(.width(32)) register_4 (.D(imm), .en(1'b1), .clk(clk), .Q(imm_o), .clr(1'b0));
  Register #(.width(22)) register_5 (.D(ctrl_A), .en(1'b1), .clk(clk), .Q(ctrl_A_o), .clr(1'b0));
  Register #(.width(12)) register_6 (.D(ctrl_B), .en(1'b1), .clk(clk), .Q(ctrl_B_o), .clr(1'b0));
  Register #(.width(5)) register_7 (.D(Rd), .en(1'b1), .clk(clk), .Q(Rd_o), .clr(1'b0));
  Register #(.width(4)) register_8 (.D(op), .en(1'b1), .clk(clk), .Q(op_o), .clr(1'b0));
  Register #(.width(5)) register_9 (.D(rs1), .en(1'b1), .clk(clk), .Q(rs1_o), .clr(1'b0));
  Register #(.width(5)) register_10 (.D(rs2), .en(1'b1), .clk(clk), .Q(rs2_o), .clr(1'b0));
  Register #(.width(1)) register_11 (.D(u_i), .en(1'b1), .clk(clk), .Q(u_o), .clr(1'b0));
endmodule

module EX_MEM (
  input  [31:0] target,
  input  clk,
  input  [31:0] ALU_res,
  input  [31:0] B,
  input  [4:0] Rd,
  input  br,
  input  [31:0] PC,
  input  ld,
  input  st,
  input  sel,
  input  [1:0] pc_sel,
  input  jal,
  output [31:0] target_o,
  output [31:0] ALU_res_o,
  output [31:0] B_o,
  output [4:0] Rd_o,
  output br_o,
  output [31:0] PC_o,
  output ld_o,
  output st_o,
  output sel_o,
  output [1:0] pc_selo,
  output jal_o
);

  Register #(.width(32)) register_1 (.D(target), .en(1'b1), .clk(clk), .Q(target_o), .clr(1'b0));
  Register #(.width(32)) register_2 (.D(ALU_res), .en(1'b1), .clk(clk), .Q(ALU_res_o), .clr(1'b0));
  Register #(.width(32)) register_3 (.D(B), .en(1'b1), .clk(clk), .Q(B_o), .clr(1'b0));
  Register #(.width(5)) register_4 (.D(Rd), .en(1'b1), .clk(clk), .Q(Rd_o), .clr(1'b0));
  Register #(.width(1)) register_5 (.D(br), .en(1'b1), .clk(clk), .Q(br_o), .clr(1'b0));
  Register #(.width(32)) register_6 (.D(PC), .en(1'b1), .clk(clk), .Q(PC_o), .clr(1'b0));
  Register #(.width(1)) register_7 (.D(ld), .en(1'b1), .clk(clk), .Q(ld_o), .clr(1'b0));
  Register #(.width(1)) register_8 (.D(st), .en(1'b1), .clk(clk), .Q(st_o), .clr(1'b0));
  Register #(.width(1)) register_9 (.D(sel), .en(1'b1), .clk(clk), .Q(sel_o), .clr(1'b0));
  Register #(.width(2)) register_10 (.D(pc_sel), .en(1'b1), .clk(clk), .Q(pc_selo), .clr(1'b0));
  Register #(.width(1)) register_11 (.D(jal), .en(1'b1), .clk(clk), .Q(jal_o), .clr(1'b0));
endmodule

module MEM_WB (
  input  clk,
  input  [31:0] D,
  input  [31:0] M,
  input  [4:0] Rd,
  input  ld,
  input  st,
  output [31:0] D_o,
  output [31:0] M_o,
  output [4:0] Rd_o,
  output ld_o,
  output st_o
);

  Register #(.width(32)) register_1 (.D(D), .en(1'b1), .clk(clk), .Q(D_o), .clr(1'b0));
  Register #(.width(32)) register_2 (.D(M), .en(1'b1), .clk(clk), .Q(M_o), .clr(1'b0));
  Register #(.width(5)) register_3 (.D(Rd), .en(1'b1), .clk(clk), .Q(Rd_o), .clr(1'b0));
  Register #(.width(1)) register_4 (.D(ld), .en(1'b1), .clk(clk), .Q(ld_o), .clr(1'b0));
  Register #(.width(1)) register_5 (.D(st), .en(1'b1), .clk(clk), .Q(st_o), .clr(1'b0));
endmodule

module decode_B (
  input  [31:0] inst,
  output [31:0] imm
);

  wire comparator_black_box_1_p4, op_inst_1_b, op_inst_1_jal, op_inst_1_jalr, op_inst_1_ld, op_inst_1_st;
  wire [1:0] inst_imm_1_o0;
  wire [19:0] shifter_1_out;
  wire [31:0] bit_extender_1_out, bit_extender_2_out, bit_extender_3_out, multiplexer_1_out, subtractor_1_out;

  op_inst op_inst_1 (
    .op(inst[6:0]), .LD(op_inst_1_ld), .ST(op_inst_1_st), .JAL(op_inst_1_jal), .JALR(op_inst_1_jalr),
    .B(op_inst_1_b));
  Shifter #(.width(20), .shift("ar")) shifter_1 (.in(inst[31:12]), .\dist (5'b01000), .out(shifter_1_out));
  inst_imm inst_imm_1 (
    .LD(op_inst_1_ld), .ST(op_inst_1_st), .JAL(op_inst_1_jal), .JALR(op_inst_1_jalr), .B(op_inst_1_b),
    .o0(inst_imm_1_o0[0]), .o1(inst_imm_1_o0[1]));
  assign bit_extender_1_out = {{12{shifter_1_out[19]}}, shifter_1_out};  // Bit_Extender bit_extender_1
  // Comparator_Black_Box comparator_black_box_1: pin names not known; wires that end beside it: bit_extender_1_out, {32{1'b0}}, 1'b1, comparator_black_box_1_p4
  Subtractor #(.width(32)) subtractor_1 (.a(bit_extender_1_out), .b(32'h1), .out(subtractor_1_out));  // open: bin, bout
  assign bit_extender_2_out = {{20{inst[31]}}, inst[31:20]};  // Bit_Extender bit_extender_2
  assign bit_extender_3_out = {{20{inst[31]}}, {inst[31:25], inst[11:7]}};  // Bit_Extender bit_extender_3
  Multiplexer #(.width(32), .enable("false")) multiplexer_1 (
    .in0(bit_extender_1_out), .in1(subtractor_1_out), .out(multiplexer_1_out), .sel(comparator_black_box_1_p4));
  Multiplexer #(.select(2), .width(32), .enable("false")) multiplexer_2 (
    .in0(bit_extender_3_out), .in1(bit_extender_2_out), .in2(multiplexer_1_out), .out(imm),
    .sel(inst_imm_1_o0));  // open: in3
endmodule

module op_inst (
  input  [6:0] op,
  output LD,
  output ST,
  output JAL,
  output JALR,
  output B
);

  wire not_1_out, not_2_out, not_3_out, not_4_out;

  not not_1 (not_1_out, op[4]);
  not not_2 (not_2_out, op[5]);
  not not_3 (not_3_out, op[3]);
  not not_4 (not_4_out, op[2]);
  and and_1 (LD, not_1_out, not_2_out);
  and and_2 (JALR, op[2], not_3_out);
  and and_3 (B, not_4_out, op[5]);

  assign JAL = op[3];
  assign ST = op[4];
endmodule

module inst_imm (
  input  LD,
  input  ST,
  input  JAL,
  input  JALR,
  input  B,
  output o0,
  output o1
);

  wire not_1_out, not_2_out, not_3_out;

  not not_1 (not_1_out, ST);
  not not_2 (not_2_out, JAL);
  not not_3 (not_3_out, B);
  and and_1 (o0, not_1_out, not_2_out, not_3_out);

  assign o1 = JAL;
endmodule

module or_12 (
  input  [11:0] in_1,
  output out_2
);

  or or_1 (out_2, in_1[0], in_1[1], in_1[2], in_1[3], in_1[4], in_1[5], in_1[6], in_1[7], in_1[8], in_1[9], in_1[10], in_1[11]);
endmodule

module B_Conds (
  input  EQ,
  input  NE,
  input  LT,
  input  GE,
  input  LTU,
  input  GEU,
  input  g,
  input  e,
  output o
);

  wire and_1_out, and_2_out, and_3_out, and_4_out, and_5_out, and_6_out, and_7_out, and_8_out, and_9_out,
       not_1_out, not_2_out, not_3_out, not_4_out, not_5_out, not_6_out, not_7_out, not_8_out, not_9_out,
       not_10_out, not_11_out, not_12_out, not_13_out, not_14_out, not_15_out, not_16_out, not_17_out,
       not_18_out, not_19_out, not_20_out, not_21_out, not_22_out, not_23_out, not_24_out, not_25_out,
       not_26_out, not_27_out, not_28_out, not_29_out, not_30_out, not_31_out, not_32_out, not_33_out;

  not not_1 (not_1_out, NE);
  not not_2 (not_2_out, LT);
  not not_3 (not_3_out, LTU);
  not not_4 (not_4_out, EQ);
  not not_5 (not_5_out, LT);
  not not_6 (not_6_out, LTU);
  not not_7 (not_7_out, EQ);
  not not_8 (not_8_out, GE);
  not not_9 (not_9_out, GEU);
  not not_10 (not_10_out, g);
  not not_11 (not_11_out, e);
  not not_12 (not_12_out, NE);
  not not_13 (not_13_out, LT);
  not not_14 (not_14_out, LTU);
  not not_15 (not_15_out, EQ);
  not not_16 (not_16_out, LT);
  not not_17 (not_17_out, LTU);
  not not_18 (not_18_out, EQ);
  not not_19 (not_19_out, GE);
  not not_20 (not_20_out, GEU);
  not not_21 (not_21_out, g);
  not not_22 (not_22_out, e);
  not not_23 (not_23_out, EQ);
  not not_24 (not_24_out, GE);
  not not_25 (not_25_out, GEU);
  not not_26 (not_26_out, g);
  not not_27 (not_27_out, e);
  not not_28 (not_28_out, EQ);
  not not_29 (not_29_out, LT);
  not not_30 (not_30_out, LTU);
  not not_31 (not_31_out, NE);
  not not_32 (not_32_out, LT);
  not not_33 (not_33_out, LTU);
  and and_1 (and_1_out, not_1_out, not_2_out, not_3_out, GEU, e);
  and and_2 (and_2_out, not_4_out, not_5_out, not_6_out, GEU, g);
  and and_3 (and_3_out, not_7_out, not_8_out, LTU, not_9_out, not_10_out, not_11_out);
  and and_4 (and_4_out, not_12_out, not_13_out, GE, not_14_out, e);
  and and_5 (and_5_out, not_15_out, not_16_out, GE, not_17_out, g);
  and and_6 (and_6_out, not_18_out, LT, not_19_out, not_20_out, not_21_out, not_22_out);
  and and_7 (and_7_out, not_23_out, NE, not_24_out, not_25_out, not_26_out, not_27_out);
  and and_8 (and_8_out, not_28_out, NE, not_29_out, not_30_out, g);
  and and_9 (and_9_out, EQ, not_31_out, not_32_out, not_33_out, e);
  or or_1 (o, and_1_out, and_2_out, and_3_out, and_4_out, and_5_out, and_6_out, and_7_out, and_8_out, and_9_out);
endmodule
