// Logisim project FSM.circ as structural Verilog: 2 circuits, main circuit main
module main (
  input  in_1,
  input  in_2,
  output out_3
);

  wire clock_1_out;
  wire [1:0] comb_1_s_2, register_1_q;

  Register #(.width(2)) register_1 (.D(comb_1_s_2), .en(1'b1), .clk(clock_1_out), .Q(register_1_q), .clr(in_2));
  Clock clock_1 (.out(clock_1_out));
  comb comb_1 (
    .stream(in_1), .s1(register_1_q[1]), .s2(register_1_q[0]), .o(out_3), .s_1(comb_1_s_2[1]),
    .s_2(comb_1_s_2[0]));
endmodule

module comb (
  input  stream,
  input  s1,
  input  s2,
  output o,
  output s_1,
  output s_2
);

  wire not_1_out, not_2_out;

  and and_1 (o, stream, s1);
  not not_1 (not_1_out, stream);
  not not_2 (not_2_out, s1);
  and and_2 (s_1, not_1_out, s2);
  and and_3 (s_2, stream, not_2_out);
endmodule
